# Fritzing sketch nokia 5110 (saved by Fritzing 0.9.1b)
breadboards: 1

parts:
  Nokia_5110_LCD_Module1 = Nokia5110LCDModule
  D1 = Rectifier Diode
  D2 = Rectifier Diode
  R4 = Resistor [tolerance=±5% resistance=1k package=THT]
  R1 = Resistor [tolerance=±5% resistance=47 package=THT]
  R2 = Resistor [tolerance=±5% resistance=47 package=THT]
  R3 = Trimmer Potentiometer [maximum_resistance=10kΩ package=THT]
  Arduino1 = Arduino Uno (Rev3)

nets:
  N1: Nokia_5110_LCD_Module1.Grnd, Arduino1.D7
  N2: Nokia_5110_LCD_Module1.RST, D2.cathode, R2.Pin_0
  N3: Nokia_5110_LCD_Module1.D/C, D1.cathode, R1.Pin_0
  N4: Nokia_5110_LCD_Module1.6_DN_(MOSI), R3.wiper
  N5: Nokia_5110_LCD_Module1.SCLK, R4.Pin_0
  N6: Nokia_5110_LCD_Module1.LED, D1.anode, D2.anode, R3.leg2, Arduino1.GND
  N7: R4.Pin_1, R3.leg1
  N8: R2.Pin_1, Arduino1.D4

custom parts:
  : Nokia 5110 LCD with 8 pin. It's a 45mm*45mm module part. Description: The Nokia 5110 is a basic graphic LCD screen for lots of applications. It was originally intended for as a cell phone screen. This one is mounted on an easy to solder PCB. It uses the PCD8544 controller. The PCD8544 is a low power CMOS LCD controller/driver, designed to drive a graphic display of 48 rows and 84 columns. All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
  Rectifier Diode: Ageneral purpose zener diode
