# Fritzing sketch BLACK (saved by Fritzing 0.9.1b)
breadboards: 1

parts:
  Nano = Arduino Nano (Rev3.0)
  R3 = Resistor [tolerance=±5% resistance=5k package=THT]
  R2 = Resistor [tolerance=±5% resistance=5k package=THT]  # not connected
  R1 = Resistor [tolerance=±5% resistance=5k package=THT]
  R4 = Resistor [tolerance=±5% resistance=5k package=THT]
  LED5 = LED - 5mm [color="Green (570nm)" part_number=LTL2R3KGD-EM package="5 mm [THT]"]
  R5 = Resistor [tolerance=±5% resistance=150 package=THT]
  LED6 = LED - 5mm [color="Green (570nm)" part_number=LTL2R3KGD-EM package="5 mm [THT]"]
  R6 = Resistor [tolerance=±5% resistance=150 package=THT]
  LED7 = LED - 5mm [color="Green (570nm)" part_number=LTL2R3KGD-EM package="5 mm [THT]"]
  R7 = Resistor [tolerance=±5% resistance=150 package=THT]
  R9 = PHOTOCELL [part_number=Adafruit-161 package=photocell-kit]
  R10 = PHOTOCELL [part_number=Adafruit-161 package=photocell-kit]
  R11 = PHOTOCELL [part_number=Adafruit-161 package=photocell-kit]
  R12 = PHOTOCELL [part_number=Adafruit-161 package=photocell-kit]
  LED8 = smd LED [color="Green (570nm)" current=20mA package="0603 [SMD]"]
  R8 = Resistor [tolerance=±5% resistance=150 package=THT]

nets:
  N1: Nano.GND, R3.Pin_1, R1.Pin_1
  N2: Nano.D8, LED5.anode
  N3: Nano.D10, LED6.anode
  N4: Nano.D11/MOSI, LED7.anode
  N5: Nano.D12/MISO, LED8.anode
  N6: Nano.5V, R9.P$2, R11.P$2, R12.P$2
  N7: Nano.A3, R9.P$1
  N8: Nano.A2, R10.P$1
  N9: Nano.A1, R3.Pin_0
  N10: Nano.A0, R4.Pin_0
  N11: LED5.cathode, R5.Pin_0
  N12: R5.Pin_1, R7.Pin_1, R8.Pin_1
  N13: LED6.cathode, R6.Pin_0
  N14: LED7.cathode, R7.Pin_0
