# Fritzing sketch RED (saved by Fritzing 0.9.1b)
circuit board: 6.74384cm x 3.9143cm
breadboards: 1

parts:
  LED1 = LED - 5mm [color="Green (570nm)" current=2mA part_number=LTL2R3KGD-EM package="5 mm [THT]"]
  LED2 = LED - 5mm [color="Green (570nm)" part_number=LTL2R3KGD-EM package="5 mm [THT]"]
  LED3 = LED - 5mm [color="Green (570nm)" part_number=LTL2R3KGD-EM package="5 mm [THT]"]
  LED4 = LED - 5mm [color="Green (570nm)" part_number=LTL2R3KGD-EM package="5 mm [THT]"]
  Nano = Arduino Nano (Rev3.0)
  R3 = Resistor [tolerance=±5% resistance=1.6k package=THT]
  R2 = Resistor [tolerance=±5% resistance=1.6k package=THT]
  R1 = Resistor [tolerance=±5% resistance=1.6k package=THT]
  R4 = Resistor [tolerance=±5% resistance=1.6k package=THT]
  R5 = Resistor [tolerance=±5% resistance=150 package=THT]
  R6 = Resistor [tolerance=±5% resistance=150 package=THT]
  R7 = Resistor [tolerance=±5% resistance=150 package=THT]
  R8 = Resistor [tolerance=±5% resistance=150 package=THT]
  LED5 = LED - 3mm [color="Green (555nm)" current=20mA part_number=RL3-G3530 package="3 mm [THT]"]
  LED6 = LED - 3mm [color="Green (555nm)" current=20mA part_number=RL3-G3530 package="3 mm [THT]"]
  LED7 = LED - 3mm [color="Green (555nm)" current=20mA part_number=RL3-G3530 package="3 mm [THT]"]
  LED8 = LED - 3mm [color="Green (555nm)" current=20mA part_number=RL3-G3530 package="3 mm [THT]"]

nets:
  N1: LED1.cathode, R1.Pin_0
  N2: LED1.anode, Nano.D3
  N3: LED2.cathode, R2.Pin_0
  N4: LED2.anode, Nano.D5
  N5: LED3.cathode, R3.Pin_0
  N6: LED3.anode, Nano.D6
  N7: LED4.cathode, R4.Pin_0
  N8: LED4.anode, Nano.D9
  N9: Nano.GND, R3.Pin_1, R2.Pin_1, R1.Pin_1, R4.Pin_1, R5.Pin_1, R6.Pin_1, R7.Pin_1, R8.Pin_1
  N10: Nano.D8, LED5.anode
  N11: Nano.D10, LED6.anode
  N12: Nano.D11/MOSI, LED7.anode
  N13: Nano.D12/MISO, LED8.anode
  N14: R5.Pin_0, LED5.cathode
  N15: R6.Pin_0, LED6.cathode
  N16: R7.Pin_0, LED7.cathode
