# Fritzing sketch receiver (saved by Fritzing 0.9.1b)
circuit board: 8.46667cm x 5.64444cm
breadboards: 1

parts:
  U2 = RF-LINK_RX [package=rf-link_rx]
  U3 = TEMPERATURE-SENSOR [package=to-92]
  Part1 = Arduino Nano (Rev3.0) (ICSP)
  LED1 = LED - 5mm [color="Red (633nm)" package="5 mm [THT]"]
  R1 = Resistor [tolerance=±5% resistance=1.5 package=THT]

nets:
  GND: U2.GND, U3.GND, Part1.GND, LED1.cathode
  N1: U2.DATA, Part1.D11/MOSI
  +5V: U2.+5V, U3.VCC, Part1.5V
  N2: U3.ADJ, Part1.A0
  N3: Part1.D1/TX, R1.Pin_0
  N4: LED1.anode, R1.Pin_1
