# Fritzing sketch transmitter (saved by Fritzing 0.9.1b)
breadboards: 1

parts:
  Part1 = Arduino Nano (Rev3.0) (ICSP)
  Part2 = Adafruit BME280
  S1 = Momentary Switch [package=ksa_sealed_tac_switch]
  U1 = RF-LINK_TX [package=rf-link_tx]

nets:
  GND: Part1.GND, Part2.GND, S1.2, U1.GND
  N1: Part1.D3, S1.1
  N2: Part1.D12/MISO, U1.DATA
  N3: Part1.A5, Part2.SCK/SCL
  N4: Part1.A4, Part2.SDI/SDA
  VIN: Part2.VIN, U1.+5V

custom parts:
  Adafruit BME280: Bosch has stepped up their game with their new BME280 sensor, an environmental sensor with temperature, barometric pressure and humidity! This sensor is great for all sorts of weather/environmental sensing and can even be used in both I2C and SPI! This precision sensor from Bosch is the best low-cost sensing solution for measuring humidity with ±3% accuracy, barometric pressure with ±1 hPa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
